# Fritzing sketch ブレッドボード (saved by Fritzing 0.9.5d)
breadboards: 1

parts:
  パーツ1 = Arduino Mega 2560 (Rev3)
  パーツ2 = Bluetooth HM-10

nets:
  5V: パーツ1.5V, パーツ2.VCC
  GND: パーツ1.GND, パーツ2.GND
  N1: パーツ1.D0_RX0, パーツ2.TXD
  N2: パーツ1.D1_TX0, パーツ2.RXD
