# Fritzing sketch ブレッドボード_ATコマンド (saved by Fritzing 0.9.5d)
breadboards: 1

parts:
  パーツ1 = Arduino Mega 2560 (Rev3)
  パーツ2 = Bluetooth HM-10

nets:
  N1: パーツ1.D11_PWM, パーツ2.RXD
  N2: パーツ1.D10_PWM, パーツ2.TXD
  5V: パーツ1.5V, パーツ2.VCC
  GND: パーツ1.GND, パーツ2.GND
